# Fritzing sketch sprinkler (saved by Fritzing 0.9.3b)
circuit board: 11.4441cm x 6.95677cm
breadboards: 1

parts:
  Master = Inductor [package="1206 [SMD]"]
  NEXT = Momentary Switch [package=tactile-pth]
  MENU = Momentary Switch [package=tactile-pth]
  PREV = Momentary Switch [package=tactile-pth]
  R2 = Resistor [tolerance=±5% resistance=220 package=THT]
  U11 = ESP8266 WiFi Module [part_number=ESP8266]
  Q1 = PNP-Transistor [package="TO92 [THT]"]
  U6 = TRIAC [package=to-92]
  U12 = TRIAC [package=to-92]
  R3 = Resistor [tolerance=±5% resistance=220 package=THT]
  Zone_1 = Inductor [package="1206 [SMD]"]
  Q2 = PNP-Transistor [package="TO92 [THT]"]
  U13 = TRIAC [package=to-92]
  R4 = Resistor [tolerance=±5% resistance=220 package=THT]
  Zone_2 = Inductor [package="1206 [SMD]"]
  Q3 = PNP-Transistor [package="TO92 [THT]"]
  U14 = TRIAC [package=to-92]
  R5 = Resistor [tolerance=±5% resistance=220 package=THT]
  Zone_3 = Inductor [package="1206 [SMD]"]
  Q4 = PNP-Transistor [package="TO92 [THT]"]
  U15 = TRIAC [package=to-92]
  R6 = Resistor [tolerance=±5% resistance=220 package=THT]
  Zone_4 = Inductor [package="1206 [SMD]"]
  Q5 = PNP-Transistor [package="TO92 [THT]"]
  U16 = TRIAC [package=to-92]
  R7 = Resistor [tolerance=±5% resistance=220 package=THT]
  Zone_5 = Inductor [package="1206 [SMD]"]
  Q6 = PNP-Transistor [package="TO92 [THT]"]
  U17 = TRIAC [package=to-92]
  R8 = Resistor [tolerance=±5% resistance=220 package=THT]
  Zone_6 = Inductor [package="1206 [SMD]"]
  Q7 = PNP-Transistor [package="TO92 [THT]"]
  U18 = TRIAC [package=to-92]
  R9 = Resistor [tolerance=±5% resistance=220 package=THT]
  Zone_7 = Inductor [package="1206 [SMD]"]
  Q8 = PNP-Transistor [package="TO92 [THT]"]
  U19 = TRIAC [package=to-92]
  R10 = Resistor [tolerance=±5% resistance=220 package=THT]
  Zone_8 = Inductor [package="1206 [SMD]"]
  Q9 = PNP-Transistor [package="TO92 [THT]"]
  U20 = TRIAC [package=to-92]
  R11 = Resistor [tolerance=±5% resistance=220 package=THT]
  Zone_9 = Inductor [package="1206 [SMD]"]
  Q10 = PNP-Transistor [package="TO92 [THT]"]
  U21 = TRIAC [package=to-92]
  R12 = Resistor [tolerance=±5% resistance=220 package=THT]
  Zone_10 = Inductor [package="1206 [SMD]"]
  Q11 = PNP-Transistor [package="TO92 [THT]"]
  Rain_Sensor = Screw terminal - 2 pins [package=THT]
  1602_I2C_LCD = Grove OLED 128x96
  U23 = V18ZA2P [package=v18za2p]
  U24 = V18ZA2P [package=v18za2p]
  U25 = V18ZA2P [package=v18za2p]
  U26 = V18ZA2P [package=v18za2p]
  U27 = V18ZA2P [package=v18za2p]
  U28 = V18ZA2P [package=v18za2p]
  U29 = V18ZA2P [package=v18za2p]
  U30 = V18ZA2P [package=v18za2p]
  U31 = V18ZA2P [package=v18za2p]
  U32 = V18ZA2P [package=v18za2p]
  U33 = V18ZA2P [package=v18za2p]
  DS3 = DS18B20 1-Wire Temperature Sensor [part_number=DS18B20]
  R13 = Resistor [tolerance=±5% resistance=4.7k package=THT]
  U34 = PCF8574 [package="DIP16 [THT]"]
  U35 = PCF8574 [package="DIP16 [THT]"]
  U36 = MOC3031-M [package=dil06]
  U37 = TRIAC [package=to-92]
  R14 = Resistor [tolerance=±5% resistance=1k package=THT]
  R15 = Resistor [tolerance=±5% resistance=220 package=THT]
  120_VAC_Transformer = Screw terminal - 2 pins [package=THT]

nets (from the schematic view):
  N1: Master.pin_0, U6.M2, U23.P$2
  24V: Master.pin_1, Zone_1.pin_1, Zone_2.pin_1, Zone_3.pin_1, Zone_4.pin_1, Zone_5.pin_1, Zone_6.pin_1, Zone_7.pin_1, Zone_8.pin_1, Zone_9.pin_1, Zone_10.pin_1
  GND: NEXT.1, MENU.1, PREV.1, U11.GND, U6.M1, U12.M1, U13.M1, U14.M1, U15.M1, U16.M1, U17.M1, U18.M1, U19.M1, U20.M1, U21.M1, Rain_Sensor.pin2, 1602_I2C_LCD.GND, U23.P$1, U24.P$1, U25.P$1, U26.P$1, U27.P$1, U28.P$1, U29.P$1, U30.P$1, U31.P$1, U32.P$1, U33.P$1, DS3.GND, U34.A0, U34.A1, U34.A3, U34.GND, U35.A1, U35.A3, U35.GND
  N2: NEXT.3, U34.P0
  N3: MENU.3, U34.P1
  N4: PREV.3, U34.P2
  N5: R2.Pin_0, U34.P7
  N6: R2.Pin_1, Q1.B
  N7: U11.RXD, DS3.DQ, R13.Pin_1
  3.3V: U11.VCC, U11.RST, U11.CH_PD, Q1.E, Q2.E, Q3.E, Q4.E, Q5.E, Q6.E, Q7.E, Q8.E, Q9.E, Q10.E, Q11.E, DS3.VDD, R13.Pin_0, U34.VCC, U35.A0, U35.VCC, R15.Pin_0
  N8: U11.GPIO_0, 1602_I2C_LCD.SCL, U34.SCL, U35.SCL
  N9: U11.GPIO_2, 1602_I2C_LCD.SDA, U34.SDA, U35.SDA
  N10: Q1.C, U6.G
  N11: U12.G, Q2.C
  N12: U12.M2, Zone_1.pin_0, U24.P$2
  N13: R3.Pin_0, U34.P6
  N14: R3.Pin_1, Q2.B
  N15: U13.G, Q3.C
  N16: U13.M2, Zone_2.pin_0, U25.P$2
  N17: R4.Pin_0, U34.P5
  N18: R4.Pin_1, Q3.B
  N19: U14.G, Q4.C
  N20: U14.M2, Zone_3.pin_0, U26.P$2
  N21: R5.Pin_0, U34.P4
  N22: R5.Pin_1, Q4.B
  N23: U15.G, Q5.C
  N24: U15.M2, Zone_4.pin_0, U27.P$2
  N25: R6.Pin_0, U35.P7
  N26: R6.Pin_1, Q5.B
  N27: U16.G, Q6.C
  N28: U16.M2, Zone_5.pin_0, U28.P$2
  N29: R7.Pin_0, U35.P6
  N30: R7.Pin_1, Q6.B
  N31: U17.G, Q7.C
  N32: U17.M2, Zone_6.pin_0, U33.P$2
  N33: R8.Pin_0, U35.P5
  N34: R8.Pin_1, Q7.B
  N35: U18.G, Q8.C
  N36: U18.M2, Zone_7.pin_0, U32.P$2
  N37: R9.Pin_0, U35.P4
  N38: R9.Pin_1, Q8.B
  N39: U19.G, Q9.C
  N40: U19.M2, Zone_8.pin_0, U31.P$2
  N41: R10.Pin_0, U35.P3
  N42: R10.Pin_1, Q9.B
  N43: U20.G, Q10.C
  N44: U20.M2, Zone_9.pin_0, U30.P$2
  N45: R11.Pin_0, U35.P2
  N46: R11.Pin_1, Q10.B
  N47: U21.G, Q11.C
  N48: U21.M2, Zone_10.pin_0, U29.P$2
  N49: R12.Pin_0, U35.P1
  N50: R12.Pin_1, Q11.B
  N51: Rain_Sensor.pin1, U34.P3
  5V: 1602_I2C_LCD.VCC
  N52: U35.P0, U36.2
  N53: U36.1, R15.Pin_1
  N54: U36.4, R14.Pin_0
  N55: U36.6, U37.M2, 120_VAC_Transformer.pin1
  N56: U37.M1, 120_VAC_Transformer.pin2
  N57: U37.G, R14.Pin_1

custom parts:
  ESP8266 WiFi Module: Generic WiFi Module based on the ESP8266 with onboard PCB antenna and UART communications
